// Logisim project W_Computer.circ as structural Verilog: 29 circuits, main circuit CPU
module main (
  input  [30:0] A,
  input  [30:0] B,
  input  in_3,
  input  in_4,
  output [30:0] OUTPUT,
  output Negative_FLAG,
  output Carry_FLAG,
  output Overflow_FLAG,
  output Zero_FLAG
);

  wire ADD_out, AND_out, button_manipulation_1_out_5, button_manipulation_1_out_8,
       button_manipulation_1_out_9, button_manipulation_1_out_10, Clk_out, d_ff_1_q, d_ff_1_qn, OR_out,
       SUBTRACT_out;
  wire [1:0] button_manipulation_1_out_7;

  Button AND (.out(AND_out));
  Button OR (.out(OR_out));
  Button ADD (.out(ADD_out));
  Button SUBTRACT (.out(SUBTRACT_out));
  Clock Clk (.out(Clk_out));
  D_Flip_Flop d_ff_1 (.clk(Clk_out), .D(in_3), .Q(d_ff_1_q), .Qn(d_ff_1_qn), .preset(in_4));  // open: en, reset
  BUTTON_Manipulation button_manipulation_1 (
    .in_1(SUBTRACT_out), .in_2(ADD_out), .in_3(OR_out), .in_4(AND_out),
    .out_6(button_manipulation_1_out_7[1]), .out_7(button_manipulation_1_out_7[0]),
    .out_5(button_manipulation_1_out_5), .out_8(button_manipulation_1_out_8),
    .out_9(button_manipulation_1_out_9), .out_10(button_manipulation_1_out_10));
  _31_BIT_ALU u_31_bit_alu_1 (
    .in_2(A), .in_3(B), .in_1(button_manipulation_1_out_7), .out_5(Zero_FLAG), .out_6(Overflow_FLAG),
    .out_7(Carry_FLAG), .out_8(Negative_FLAG), .out_4(OUTPUT));
  LED AND_2 (.in(button_manipulation_1_out_5));
  LED OR_2 (.in(button_manipulation_1_out_8));
  LED ADD_2 (.in(button_manipulation_1_out_9));
  LED SUB (.in(button_manipulation_1_out_10));
endmodule

// BTN
module BUTTON_Manipulation (
  input  in_1,
  input  in_2,
  input  in_3,
  input  in_4,
  output out_5,
  output out_6,
  output out_7,
  output out_8,
  output out_9,
  output out_10
);

  wire d_ff_1_q, d_ff_2_q, d_ff_3_q, d_ff_4_q, d_ff_5_q, d_ff_6_q, d_ff_7_q, d_ff_8_q, not_1_out, not_2_out,
       or_1_out, or_3_out, or_4_out, or_6_out;

  D_Flip_Flop d_ff_1 (.clk(in_1), .D(1'b1), .Q(d_ff_1_q), .reset(or_1_out));  // open: Qn, preset, en
  D_Flip_Flop d_ff_2 (.clk(in_1), .D(1'b1), .Q(d_ff_2_q), .reset(or_1_out));  // open: Qn, preset, en
  or or_1 (or_1_out, in_4, in_3, in_2);
  or or_2 (out_6, d_ff_1_q, d_ff_3_q, d_ff_5_q, d_ff_7_q);
  D_Flip_Flop d_ff_3 (.clk(in_2), .D(1'b1), .Q(d_ff_3_q), .reset(or_3_out));  // open: Qn, preset, en
  D_Flip_Flop d_ff_4 (.clk(in_2), .Q(d_ff_4_q), .reset(or_3_out));  // open: D, Qn, preset, en
  or or_3 (or_3_out, in_1, in_3, in_4);
  D_Flip_Flop d_ff_5 (.clk(in_3), .Q(d_ff_5_q), .reset(or_4_out));  // open: D, Qn, preset, en
  or or_4 (or_4_out, in_1, in_2, in_4);
  D_Flip_Flop d_ff_6 (.clk(in_3), .D(1'b1), .Q(d_ff_6_q), .reset(or_4_out));  // open: Qn, preset, en
  or or_5 (out_7, d_ff_4_q, d_ff_6_q, d_ff_8_q, d_ff_2_q);
  D_Flip_Flop d_ff_7 (.clk(in_4), .Q(d_ff_7_q), .reset(or_6_out));  // open: D, Qn, preset, en
  or or_6 (or_6_out, in_3, in_2, in_1);
  not not_1 (not_1_out, out_6);
  D_Flip_Flop d_ff_8 (.clk(in_4), .Q(d_ff_8_q), .reset(or_6_out));  // open: D, Qn, preset, en
  not not_2 (not_2_out, out_7);
  nor nor_1 (out_5, out_7, out_6);
  and and_1 (out_8, out_7, not_1_out);
  and and_2 (out_9, not_2_out, out_6);
  and and_3 (out_10, out_7, out_6);
endmodule

module _31_BIT_ALU (
  input  [1:0] in_1,
  input  [30:0] in_2,
  input  [30:0] in_3,
  output [30:0] out_4,
  output out_5,
  output out_6,
  output out_7,
  output out_8
);

  wire n31_bit_add_sub_er_1_out_5, n31_bit_add_sub_er_1_out_6;
  wire [30:0] n31_bit_add_sub_er_1_out_4, n31_bit_and_1_out_3, n31_bit_or_1_out_3;

  _31_BIT_AND u_31_bit_and_1 (.in_1(in_2), .in_2(in_3), .out_3(n31_bit_and_1_out_3));
  _31_BIT_OR u_31_bit_or_1 (.in_1(in_2), .in_2(in_3), .out_3(n31_bit_or_1_out_3));
  _31_BIT_ADD_SUB_ER u_31_bit_add_sub_er_1 (
    .in_2(in_2), .in_3(in_3), .in_1(in_1[0]), .out_6(n31_bit_add_sub_er_1_out_6),
    .out_4(n31_bit_add_sub_er_1_out_4), .out_5(n31_bit_add_sub_er_1_out_5));
  and and_1 (out_7, n31_bit_add_sub_er_1_out_6, in_1[1]);
  Multiplexer #(.select(2), .width(31), .enable("false")) multiplexer_1 (
    .in0(n31_bit_and_1_out_3), .in1(n31_bit_or_1_out_3), .in2(n31_bit_add_sub_er_1_out_4),
    .in3(n31_bit_add_sub_er_1_out_4), .out(out_4), .sel(in_1));
  and and_2 (out_6, n31_bit_add_sub_er_1_out_5, in_1[1]);
  ZEROFLAG_CHECK zeroflag_check_1 (.in_1(out_4), .out_2(out_5));

  assign out_8 = out_4[30];
endmodule

// ZFL
module ZEROFLAG_CHECK (
  input  [30:0] in_1,
  output out_2
);

  wire or_1_out;

  or or_1 (or_1_out, in_1[0], in_1[1], in_1[2], in_1[3], in_1[4], in_1[5], in_1[6], in_1[7], in_1[8], in_1[9], in_1[10], in_1[11], in_1[12], in_1[13], in_1[14], in_1[15], in_1[16], in_1[17], in_1[18], in_1[19], in_1[20], in_1[21], in_1[22], in_1[23], in_1[24], in_1[25], in_1[26], in_1[27], in_1[28], in_1[29], in_1[30]);
  not not_1 (out_2, or_1_out);
endmodule

// AND
module _31_BIT_AND (
  input  [30:0] in_1,
  input  [30:0] in_2,
  output [30:0] out_3
);

  assign out_3 = in_1 & in_2;  // AND_Gate and_1, 31 bits wide
endmodule

// OR
module _31_BIT_OR (
  input  [30:0] in_1,
  input  [30:0] in_2,
  output [30:0] out_3
);

  assign out_3 = in_1 | in_2;  // OR_Gate or_1, 31 bits wide
endmodule

module _1BIT_FULL_ADDER (
  input  in_1,
  input  in_2,
  input  in_3,
  output out_4,
  output out_5
);

  wire and_1_out, and_2_out, xor_1_out;

  xor xor_1 (xor_1_out, in_2, in_3);
  xor xor_2 (out_4, in_1, xor_1_out);
  and and_1 (and_1_out, in_1, xor_1_out);
  and and_2 (and_2_out, in_3, in_2);
  or or_1 (out_5, and_1_out, and_2_out);
endmodule

// ADS
module _31_BIT_ADD_SUB_ER (
  input  in_1,
  input  [30:0] in_2,
  input  [30:0] in_3,
  output [30:0] out_4,
  output out_5,
  output out_6
);

  wire [30:0] xor_1_out;

  assign xor_1_out = {31{in_1}} ^ in_3;  // XOR_Gate xor_1, 31 bits wide
  _31_BIT_CLA_ADDER u_31_bit_cla_adder_1 (
    .in_2(in_2), .in_3(xor_1_out), .in_1(in_1), .carry(out_6), .out_4(out_4), .out_5(out_5));
endmodule

module _31_BIT_CLA_ADDER (
  input  in_1,
  input  [30:0] in_2,
  input  [30:0] in_3,
  output [30:0] out_4,
  output out_5,
  output carry
);

  wire n1bit_full_adder_1_out_5, n1bit_full_adder_2_out_5, n1bit_full_adder_3_out_5,
       n4_bit_cla_adder_1_out_14, n8_bit_cla_adder_1_out_12, n8_bit_cla_adder_2_out_12,
       n8_bit_cla_adder_3_out_12, n8_bit_cla_adder_4_out_12;
  wire [7:7] not_1_out, not_2_out;

  not not_1 (not_1_out[7], 1'b1);
  not not_2 (not_2_out[7], 1'b1);
  _8_Bit_CLA_ADDER u_8_bit_cla_adder_1 (
    .in_2(in_2[7:0]), .in_3(in_3[7:0]), .in_1(in_1), .out_12(n8_bit_cla_adder_1_out_12), .out_4(out_4[0]),
    .out_5(out_4[1]), .out_6(out_4[2]), .out_7(out_4[3]), .out_8(out_4[4]), .out_9(out_4[5]),
    .out_10(out_4[6]), .out_11(out_4[7]));
  _8_Bit_CLA_ADDER u_8_bit_cla_adder_2 (
    .in_2(in_2[15:8]), .in_3(in_3[15:8]), .in_1(n8_bit_cla_adder_1_out_12),
    .out_12(n8_bit_cla_adder_2_out_12), .out_4(out_4[8]), .out_5(out_4[9]), .out_6(out_4[10]),
    .out_7(out_4[11]), .out_8(out_4[12]), .out_9(out_4[13]), .out_10(out_4[14]), .out_11(out_4[15]));
  _8_Bit_CLA_ADDER u_8_bit_cla_adder_3 (
    .in_2(in_2[23:16]), .in_3(in_3[23:16]), .in_1(n8_bit_cla_adder_2_out_12),
    .out_12(n8_bit_cla_adder_3_out_12), .out_4(out_4[16]), .out_5(out_4[17]), .out_6(out_4[18]),
    .out_7(out_4[19]), .out_8(out_4[20]), .out_9(out_4[21]), .out_10(out_4[22]), .out_11(out_4[23]));
  _8_Bit_CLA_ADDER u_8_bit_cla_adder_4 (
    .in_2({not_1_out[7], in_2[30:24]}), .in_3({not_2_out[7], in_3[30:24]}), .in_1(n8_bit_cla_adder_3_out_12),
    .out_12(n8_bit_cla_adder_4_out_12), .out_4(out_4[24]), .out_5(out_4[25]), .out_6(out_4[26]),
    .out_7(out_4[27]), .out_8(out_4[28]), .out_9(out_4[29]), .out_10(out_4[30]), .out_11(carry));
  _4_BIT_CLA_ADDER u_4_bit_cla_adder_1 (
    .in_2(in_2[24]), .in_3(in_2[25]), .in_4(in_2[26]), .in_5(in_2[27]), .in_6(in_3[24]), .in_7(in_3[25]),
    .in_8(in_3[26]), .in_9(in_3[27]), .in_1(n8_bit_cla_adder_3_out_12), .out_14(n4_bit_cla_adder_1_out_14));  // open: out_10, out_11, out_12, out_13
  _1BIT_FULL_ADDER u_1bit_full_adder_1 (
    .in_2(in_2[28]), .in_3(in_3[28]), .in_1(n4_bit_cla_adder_1_out_14), .out_5(n1bit_full_adder_1_out_5));  // open: out_4
  _1BIT_FULL_ADDER u_1bit_full_adder_2 (
    .in_2(in_2[29]), .in_3(in_3[29]), .in_1(n1bit_full_adder_1_out_5), .out_5(n1bit_full_adder_2_out_5));  // open: out_4
  _1BIT_FULL_ADDER u_1bit_full_adder_3 (
    .in_2(in_2[30]), .in_3(in_3[30]), .in_1(n1bit_full_adder_2_out_5), .out_5(n1bit_full_adder_3_out_5));  // open: out_4
  xor xor_1 (out_5, n1bit_full_adder_2_out_5, n1bit_full_adder_3_out_5);
  // also tied to GND on the sheet: n8_bit_cla_adder_4_out_12
endmodule

module _8_Bit_CLA_ADDER (
  input  in_1,
  input  [7:0] in_2,
  input  [7:0] in_3,
  output out_4,
  output out_5,
  output out_6,
  output out_7,
  output out_8,
  output out_9,
  output out_10,
  output out_11,
  output out_12
);

  wire n4_bit_cla_adder_1_out_14;

  _4_BIT_CLA_ADDER u_4_bit_cla_adder_1 (
    .in_2(in_2[0]), .in_3(in_2[1]), .in_4(in_2[2]), .in_5(in_2[3]), .in_6(in_3[0]), .in_7(in_3[1]),
    .in_8(in_3[2]), .in_9(in_3[3]), .in_1(in_1), .out_14(n4_bit_cla_adder_1_out_14), .out_10(out_4),
    .out_11(out_5), .out_12(out_6), .out_13(out_7));
  _4_BIT_CLA_ADDER u_4_bit_cla_adder_2 (
    .in_2(in_2[4]), .in_3(in_2[5]), .in_4(in_2[6]), .in_5(in_2[7]), .in_6(in_3[4]), .in_7(in_3[5]),
    .in_8(in_3[6]), .in_9(in_3[7]), .in_1(n4_bit_cla_adder_1_out_14), .out_14(out_12), .out_10(out_8),
    .out_11(out_9), .out_12(out_10), .out_13(out_11));
endmodule

module _4_BIT_CLA_ADDER (
  input  in_1,
  input  in_2,
  input  in_3,
  input  in_4,
  input  in_5,
  input  in_6,
  input  in_7,
  input  in_8,
  input  in_9,
  output out_10,
  output out_11,
  output out_12,
  output out_13,
  output out_14
);

  wire and_1_out, and_2_out, and_3_out, and_4_out, and_5_out, and_6_out, and_7_out, and_8_out, and_9_out,
       and_10_out, and_11_out, and_12_out, and_13_out, and_14_out, or_1_out, or_3_out, or_4_out, xor_1_out,
       xor_2_out, xor_3_out, xor_4_out;

  and and_1 (and_1_out, in_5, in_9);
  xor xor_1 (xor_1_out, in_2, in_6);
  and and_2 (and_2_out, in_2, in_6);
  xor xor_2 (xor_2_out, in_3, in_7);
  and and_3 (and_3_out, in_7, in_3);
  xor xor_3 (xor_3_out, in_4, in_8);
  and and_4 (and_4_out, in_4, in_8);
  xor xor_4 (xor_4_out, in_5, in_9);
  and and_5 (and_5_out, and_4_out, xor_4_out);
  and and_6 (and_6_out, in_1, xor_1_out, xor_2_out, xor_3_out, xor_4_out);
  and and_7 (and_7_out, in_1, xor_1_out, xor_2_out, xor_3_out);
  and and_8 (and_8_out, xor_4_out, xor_3_out, and_2_out, xor_2_out);
  and and_9 (and_9_out, and_2_out, xor_2_out, xor_3_out);
  and and_10 (and_10_out, and_3_out, xor_3_out);
  and and_11 (and_11_out, and_3_out, xor_4_out, xor_3_out);
  and and_12 (and_12_out, in_1, xor_1_out, xor_2_out);
  and and_13 (and_13_out, xor_2_out, and_2_out);
  or or_1 (or_1_out, and_7_out, and_9_out, and_10_out, and_4_out);
  or or_2 (out_14, and_6_out, and_8_out, and_11_out, and_5_out, and_1_out);
  and and_14 (and_14_out, in_1, xor_1_out);
  or or_3 (or_3_out, and_12_out, and_13_out, and_3_out);
  or or_4 (or_4_out, and_14_out, and_2_out);
  xor xor_5 (out_12, or_3_out, xor_3_out);
  xor xor_6 (out_10, in_1, xor_1_out);
  xor xor_7 (out_11, or_4_out, xor_2_out);
  xor xor_8 (out_13, or_1_out, xor_4_out);
endmodule

module Controller (
  input  [1:0] Q,
  input  [2:0] T,
  input  C,
  output D0,
  output D1,
  output D2
);

  wire and_1_out, and_2_out, and_3_out, and_4_out, and_5_out, or_4_out, or_5_out, Q0, Q1, Q2, Q3, T0, T1, T2,
       T3, T4, T5, T6, T7;

  or or_1 (D0, T0, and_3_out, T3, T4, and_1_out, T7);
  or or_2 (D1, T1, T5, and_4_out, T7, T6);
  or or_3 (D2, T4, and_5_out, T5, T7, T3, and_2_out);
  Decoder #(.select(2), .enable("false")) decoder_1 (.out0(Q0), .out1(Q1), .out2(Q2), .out3(Q3), .sel(Q));
  Decoder #(.select(3), .enable("false")) decoder_2 (
    .out0(T0), .out1(T1), .out2(T2), .out3(T3), .out4(T4), .out5(T5), .out6(T6), .out7(T7), .sel(T));
  and and_1 (and_1_out, T2, or_4_out);
  and and_2 (and_2_out, T6, C);
  and and_3 (and_3_out, T6, C);
  or or_4 (or_4_out, Q0, Q2, Q3);
  and and_4 (and_4_out, T2, Q2);
  and and_5 (and_5_out, T2, or_5_out);
  or or_5 (or_5_out, Q0, Q1, Q3);
endmodule

module SEQ_DECODER (
  input  CLK,
  input  Reset,
  input  Q0,
  input  Q_1,
  input  [4:0] Count,
  output Clear__A__Q_1,
  output Load__M__Q__Cnt,
  output C0,
  output C1,
  output Load_A,
  output ShiftRight,
  output Dec_Cnt
);

  wire controller_1_d0, controller_1_d1, controller_1_d2, nor_1_out, T0, T2, T4, T6, T7;
  wire [2:0] T;

  nor nor_1 (nor_1_out, Count[0], Count[1], Count[2], Count[3], Count[4]);
  Decoder #(.select(3), .enable("false")) decoder_1 (
    .out0(T0), .out1(Clear__A__Q_1), .out2(T2), .out3(C0), .out4(T4), .out5(Dec_Cnt), .out6(T6), .out7(T7),
    .sel(T));
  Controller controller_1 (
    .Q({Q0, Q_1}), .T(T), .C(nor_1_out), .D0(controller_1_d0), .D1(controller_1_d1), .D2(controller_1_d2));
  D_Flip_Flop d_ff_1 (.clk(CLK), .D(controller_1_d0), .Q(T[0]), .reset(Reset));  // open: Qn, preset, en
  D_Flip_Flop d_ff_2 (.clk(CLK), .D(controller_1_d1), .Q(T[1]), .reset(Reset));  // open: Qn, preset, en
  D_Flip_Flop d_ff_3 (.clk(CLK), .D(controller_1_d2), .Q(T[2]), .reset(Reset));  // open: Qn, preset, en
  or or_1 (C1, C0, T4);

  assign Load__M__Q__Cnt = Clear__A__Q_1;
  assign Load_A = C1;
  assign ShiftRight = Dec_Cnt;

  // Other names for the same wires on the sheet: T1 = Clear__A__Q_1; T3 = C0; T5 = Dec_Cnt
endmodule

module booths_multiplier (
  input  [30:0] M_input,
  input  [30:0] Q_input,
  input  Reset,
  output [30:0] out_4,
  output [30:0] out_5
);

  wire A_out, C0, C1, Clk, CLR, LMQC, or_1_out, Q_1, Qp, seq_decoder_1_dec_cnt, seq_decoder_1_load_a, SHR;
  wire [4:0] Ctr;
  wire [30:0] A, M, M_q30, Q;

  Clock clock_1 (.out(Clk));
  or or_1 (or_1_out, seq_decoder_1_dec_cnt, LMQC);
  Counter #(.width(5), .max('h1f)) counter_1 (
    .load(or_1_out), .D({5{1'b1}}), .count(seq_decoder_1_dec_cnt), .Q(Ctr), .clk(Clk));  // open: carry, clr
  _2s_complement u_2s_complement_1 (.Input(M_input), .Output(M));
  _2s_complement u_2s_complement_2 (.Input(Q_input), .Output(Q));
  SEQ_DECODER seq_decoder_1 (
    .CLK(Clk), .Reset(Reset), .Q0(out_5[0]), .Q_1(Q_1), .Count(Ctr), .Clear__A__Q_1(CLR),
    .Load__M__Q__Cnt(LMQC), .C0(C0), .C1(C1), .Load_A(seq_decoder_1_load_a), .ShiftRight(SHR),
    .Dec_Cnt(seq_decoder_1_dec_cnt));
  Shift_Register #(.length(31)) u_M (
    .shift(1'b0), .clk(Clk), .load(LMQC), .d0(M[30]), .q0(M_q30[30]), .d1(M[29]), .q1(M_q30[29]), .d2(M[28]),
    .q2(M_q30[28]), .d3(M[27]), .q3(M_q30[27]), .d4(M[26]), .q4(M_q30[26]), .d5(M[25]), .q5(M_q30[25]),
    .d6(M[24]), .q6(M_q30[24]), .d7(M[23]), .q7(M_q30[23]), .d8(M[22]), .q8(M_q30[22]), .d9(M[21]),
    .q9(M_q30[21]), .d10(M[20]), .q10(M_q30[20]), .d11(M[19]), .q11(M_q30[19]), .d12(M[18]), .q12(M_q30[18]),
    .d13(M[17]), .q13(M_q30[17]), .d14(M[16]), .q14(M_q30[16]), .d15(M[15]), .q15(M_q30[15]), .d16(M[14]),
    .q16(M_q30[14]), .d17(M[13]), .q17(M_q30[13]), .d18(M[12]), .q18(M_q30[12]), .d19(M[11]),
    .q19(M_q30[11]), .d20(M[10]), .q20(M_q30[10]), .d21(M[9]), .q21(M_q30[9]), .d22(M[8]), .q22(M_q30[8]),
    .d23(M[7]), .q23(M_q30[7]), .d24(M[6]), .q24(M_q30[6]), .d25(M[5]), .q25(M_q30[5]), .d26(M[4]),
    .q26(M_q30[4]), .d27(M[3]), .q27(M_q30[3]), .d28(M[2]), .q28(M_q30[2]), .d29(M[1]), .q29(M_q30[1]),
    .d30(M[0]), .q30(M_q30[0]));  // open: in, out, clr
  Shift_Register #(.length(31)) u_A (
    .shift(SHR), .in(out_4[30]), .clk(Clk), .out(A_out), .load(seq_decoder_1_load_a), .clr(CLR), .d0(A[30]),
    .q0(out_4[30]), .d1(A[29]), .q1(out_4[29]), .d2(A[28]), .q2(out_4[28]), .d3(A[27]), .q3(out_4[27]),
    .d4(A[26]), .q4(out_4[26]), .d5(A[25]), .q5(out_4[25]), .d6(A[24]), .q6(out_4[24]), .d7(A[23]),
    .q7(out_4[23]), .d8(A[22]), .q8(out_4[22]), .d9(A[21]), .q9(out_4[21]), .d10(A[20]), .q10(out_4[20]),
    .d11(A[19]), .q11(out_4[19]), .d12(A[18]), .q12(out_4[18]), .d13(A[17]), .q13(out_4[17]), .d14(A[16]),
    .q14(out_4[16]), .d15(A[15]), .q15(out_4[15]), .d16(A[14]), .q16(out_4[14]), .d17(A[13]),
    .q17(out_4[13]), .d18(A[12]), .q18(out_4[12]), .d19(A[11]), .q19(out_4[11]), .d20(A[10]),
    .q20(out_4[10]), .d21(A[9]), .q21(out_4[9]), .d22(A[8]), .q22(out_4[8]), .d23(A[7]), .q23(out_4[7]),
    .d24(A[6]), .q24(out_4[6]), .d25(A[5]), .q25(out_4[5]), .d26(A[4]), .q26(out_4[4]), .d27(A[3]),
    .q27(out_4[3]), .d28(A[2]), .q28(out_4[2]), .d29(A[1]), .q29(out_4[1]), .d30(A[0]), .q30(out_4[0]));
  _31_BIT_ALU u_31_bit_alu_1 (
    .in_2(out_4), .in_3(M_q30), .in_1({C1, C0}), .out_4(A));  // open: out_5, out_6, out_7, out_8
  Shift_Register #(.length(31)) u_Q (
    .shift(SHR), .in(A_out), .clk(Clk), .out(Qp), .load(LMQC), .d0(Q[30]), .q0(out_5[30]), .d1(Q[29]),
    .q1(out_5[29]), .d2(Q[28]), .q2(out_5[28]), .d3(Q[27]), .q3(out_5[27]), .d4(Q[26]), .q4(out_5[26]),
    .d5(Q[25]), .q5(out_5[25]), .d6(Q[24]), .q6(out_5[24]), .d7(Q[23]), .q7(out_5[23]), .d8(Q[22]),
    .q8(out_5[22]), .d9(Q[21]), .q9(out_5[21]), .d10(Q[20]), .q10(out_5[20]), .d11(Q[19]), .q11(out_5[19]),
    .d12(Q[18]), .q12(out_5[18]), .d13(Q[17]), .q13(out_5[17]), .d14(Q[16]), .q14(out_5[16]), .d15(Q[15]),
    .q15(out_5[15]), .d16(Q[14]), .q16(out_5[14]), .d17(Q[13]), .q17(out_5[13]), .d18(Q[12]),
    .q18(out_5[12]), .d19(Q[11]), .q19(out_5[11]), .d20(Q[10]), .q20(out_5[10]), .d21(Q[9]), .q21(out_5[9]),
    .d22(Q[8]), .q22(out_5[8]), .d23(Q[7]), .q23(out_5[7]), .d24(Q[6]), .q24(out_5[6]), .d25(Q[5]),
    .q25(out_5[5]), .d26(Q[4]), .q26(out_5[4]), .d27(Q[3]), .q27(out_5[3]), .d28(Q[2]), .q28(out_5[2]),
    .d29(Q[1]), .q29(out_5[1]), .d30(Q[0]), .q30(out_5[0]));  // open: clr
  Shift_Register #(.length(1)) u_Q_1 (.shift(SHR), .in(Qp), .clk(Clk), .clr(CLR), .q0(Q_1));  // open: out, load, d0

  // Other names for the same wires on the sheet: Q0 = out_5[0]

  // Notes on the sheet:
  //   RESULT
endmodule

module _2s_complement (
  input  [30:0] Input,
  output [30:0] Output
);

  wire [29:0] not_1_out;
  wire [30:0] bit_extender_1_out, n31_bit_alu_1_out_4;

  assign bit_extender_1_out = {{30{1'b0}}, 1'b1};  // Bit_Extender bit_extender_1
  not not_1 (not_1_out[0], Input[0]);
  not not_2 (not_1_out[1], Input[1]);
  not not_3 (not_1_out[2], Input[2]);
  not not_4 (not_1_out[3], Input[3]);
  not not_5 (not_1_out[4], Input[4]);
  not not_6 (not_1_out[5], Input[5]);
  not not_7 (not_1_out[6], Input[6]);
  not not_8 (not_1_out[7], Input[7]);
  not not_9 (not_1_out[8], Input[8]);
  not not_10 (not_1_out[9], Input[9]);
  not not_11 (not_1_out[10], Input[10]);
  not not_12 (not_1_out[11], Input[11]);
  not not_13 (not_1_out[12], Input[12]);
  not not_14 (not_1_out[13], Input[13]);
  not not_15 (not_1_out[14], Input[14]);
  not not_16 (not_1_out[15], Input[15]);
  not not_17 (not_1_out[16], Input[16]);
  not not_18 (not_1_out[17], Input[17]);
  not not_19 (not_1_out[18], Input[18]);
  not not_20 (not_1_out[19], Input[19]);
  not not_21 (not_1_out[20], Input[20]);
  not not_22 (not_1_out[21], Input[21]);
  not not_23 (not_1_out[22], Input[22]);
  not not_24 (not_1_out[23], Input[23]);
  not not_25 (not_1_out[24], Input[24]);
  not not_26 (not_1_out[25], Input[25]);
  not not_27 (not_1_out[26], Input[26]);
  not not_28 (not_1_out[27], Input[27]);
  not not_29 (not_1_out[28], Input[28]);
  not not_30 (not_1_out[29], Input[29]);
  _31_BIT_ALU u_31_bit_alu_1 (
    .in_2({Input[30], not_1_out}), .in_3(bit_extender_1_out), .in_1(2'b10), .out_4(n31_bit_alu_1_out_4));  // open: out_5, out_6, out_7, out_8
  Multiplexer #(.width(31), .enable("false")) multiplexer_1 (
    .in0(Input), .in1(n31_bit_alu_1_out_4), .out(Output), .sel(Input[30]));
endmodule

module _2_BIT_Parallel_LOAD_REG (
  input  load,
  input  [1:0] l1,
  input  Clk,
  input  Clr,
  output [1:0] out
);

  wire and_1_out, and_2_out, and_3_out, and_4_out, not_1_out, not_2_out, or_1_out, or_2_out;

  not not_1 (not_1_out, load);
  not not_2 (not_2_out, not_1_out);
  and and_1 (and_1_out, not_2_out, l1[0]);
  and and_2 (and_2_out, out[0], not_1_out);
  and and_3 (and_3_out, not_1_out, out[1]);
  and and_4 (and_4_out, not_2_out, l1[1]);
  or or_1 (or_1_out, and_1_out, and_2_out);
  or or_2 (or_2_out, and_3_out, and_4_out);
  D_Flip_Flop d_ff_1 (.clk(Clk), .D(or_1_out), .Q(out[0]), .reset(Clr));  // open: Qn, preset, en
  D_Flip_Flop d_ff_2 (.clk(Clk), .D(or_2_out), .Q(out[1]), .reset(Clr));  // open: Qn, preset, en
  // Probe on out
endmodule

module _3_BIT_Parallel_LD_REG (
  input  LOAD,
  input  [2:0] L1,
  input  CLK,
  input  CLR,
  output [2:0] out
);

  wire and_1_out, and_2_out, and_3_out, and_4_out, and_5_out, and_6_out, not_1_out, not_2_out, or_1_out,
       or_2_out, or_3_out;

  not not_1 (not_1_out, LOAD);
  not not_2 (not_2_out, not_1_out);
  and and_1 (and_1_out, not_2_out, L1[0]);
  and and_2 (and_2_out, out[0], not_1_out);
  and and_3 (and_3_out, not_1_out, out[1]);
  and and_4 (and_4_out, not_2_out, L1[1]);
  and and_5 (and_5_out, not_1_out, out[2]);
  and and_6 (and_6_out, not_2_out, L1[2]);
  or or_1 (or_1_out, and_1_out, and_2_out);
  or or_2 (or_2_out, and_5_out, and_6_out);
  or or_3 (or_3_out, and_3_out, and_4_out);
  D_Flip_Flop d_ff_1 (.clk(CLK), .D(or_1_out), .Q(out[0]), .reset(CLR));  // open: Qn, preset, en
  D_Flip_Flop d_ff_2 (.clk(CLK), .D(or_3_out), .Q(out[1]), .reset(CLR));  // open: Qn, preset, en
  D_Flip_Flop d_ff_3 (.clk(CLK), .D(or_2_out), .Q(out[2]), .reset(CLR));  // open: Qn, preset, en
  // Probe on out
endmodule

module IR (
  input  LOAD,
  input  [3:0] L1,
  input  CLK,
  input  CLR,
  output [3:0] out
);

  wire and_1_out, and_2_out, and_3_out, and_4_out, and_5_out, and_6_out, and_7_out, and_8_out, not_1_out,
       not_2_out, or_1_out, or_2_out, or_3_out, or_4_out;

  not not_1 (not_1_out, LOAD);
  not not_2 (not_2_out, not_1_out);
  and and_1 (and_1_out, not_2_out, L1[0]);
  and and_2 (and_2_out, out[0], not_1_out);
  and and_3 (and_3_out, not_1_out, out[1]);
  and and_4 (and_4_out, not_2_out, L1[1]);
  and and_5 (and_5_out, not_1_out, out[2]);
  and and_6 (and_6_out, not_2_out, L1[2]);
  and and_7 (and_7_out, not_1_out, out[3]);
  and and_8 (and_8_out, not_2_out, L1[3]);
  or or_1 (or_1_out, and_1_out, and_2_out);
  or or_2 (or_2_out, and_3_out, and_4_out);
  or or_3 (or_3_out, and_5_out, and_6_out);
  or or_4 (or_4_out, and_7_out, and_8_out);
  D_Flip_Flop d_ff_1 (.clk(CLK), .D(or_1_out), .Q(out[0]), .reset(CLR));  // open: Qn, preset, en
  D_Flip_Flop d_ff_2 (.clk(CLK), .D(or_2_out), .Q(out[1]), .reset(CLR));  // open: Qn, preset, en
  D_Flip_Flop d_ff_3 (.clk(CLK), .D(or_3_out), .Q(out[2]));  // open: Qn, preset, en, reset
  D_Flip_Flop d_ff_4 (.clk(CLK), .D(or_4_out), .Q(out[3]));  // open: Qn, preset, en, reset
  // Probe on out
endmodule

module MAR (
  input  LOAD,
  input  [5:0] IN,
  input  CLK,
  input  Clr,
  output [5:0] out_5
);

  _3_BIT_Parallel_LD_REG u_3_bit_parallel_ld_reg_1 (.LOAD(LOAD), .L1(IN[2:0]), .CLK(CLK), .CLR(Clr), .out(out_5[2:0]));
  _3_BIT_Parallel_LD_REG u_3_bit_parallel_ld_reg_2 (.LOAD(LOAD), .L1(IN[5:3]), .CLK(CLK), .CLR(Clr), .out(out_5[5:3]));
endmodule

module AC (
  input  LOAD,
  input  [30:0] IN,
  input  CLK,
  input  CLR,
  output [30:0] out_5
);

  IR ir_1 (.LOAD(LOAD), .L1(IN[3:0]), .CLK(CLK), .CLR(CLR), .out(out_5[3:0]));
  IR ir_2 (.LOAD(LOAD), .L1(IN[7:4]), .CLK(CLK), .CLR(CLR), .out(out_5[7:4]));
  IR ir_3 (.LOAD(LOAD), .L1(IN[11:8]), .CLK(CLK), .CLR(CLR), .out(out_5[11:8]));
  IR ir_4 (.LOAD(LOAD), .L1(IN[15:12]), .CLK(CLK), .CLR(CLR), .out(out_5[15:12]));
  IR ir_5 (.LOAD(LOAD), .L1(IN[19:16]), .CLK(CLK), .CLR(CLR), .out(out_5[19:16]));
  IR ir_6 (.LOAD(LOAD), .L1(IN[23:20]), .CLK(CLK), .CLR(CLR), .out(out_5[23:20]));
  IR ir_7 (.LOAD(LOAD), .L1(IN[27:24]), .CLK(CLK), .CLR(CLR), .out(out_5[27:24]));
  _3_BIT_Parallel_LD_REG u_3_bit_parallel_ld_reg_1 (
    .LOAD(LOAD), .L1(IN[30:28]), .CLK(CLK), .CLR(CLR), .out(out_5[30:28]));
endmodule

module _3_BIT_Parallel_Counter (
  input  LOAD,
  input  COUNT,
  input  [2:0] IN,
  input  K,
  input  CLR,
  output [2:0] out_6,
  output Cout
);

  wire and_1_out, and_2_out, and_3_out, and_4_out, and_5_out, and_6_out, and_7_out, and_8_out, and_9_out,
       not_1_out, not_2_out, not_3_out, not_4_out, not_5_out, or_1_out, or_2_out, or_3_out, or_4_out,
       or_5_out, or_6_out;

  not not_1 (not_1_out, LOAD);
  not not_2 (not_2_out, not_1_out);
  and and_1 (and_1_out, not_1_out, COUNT);
  not not_3 (not_3_out, IN[2]);
  not not_4 (not_4_out, IN[0]);
  not not_5 (not_5_out, IN[1]);
  and and_2 (and_2_out, not_2_out, IN[0]);
  and and_3 (and_3_out, not_4_out, not_2_out);
  and and_4 (and_4_out, not_2_out, IN[1]);
  and and_5 (and_5_out, not_5_out, not_2_out);
  and and_6 (and_6_out, IN[2], not_2_out);
  and and_7 (and_7_out, not_2_out, not_3_out);
  or or_1 (or_1_out, and_2_out, and_1_out);
  or or_2 (or_2_out, and_3_out, and_1_out);
  and and_8 (and_8_out, and_1_out, out_6[0]);
  and and_9 (and_9_out, and_1_out, out_6[0], out_6[1]);
  or or_3 (or_3_out, and_4_out, and_8_out);
  or or_4 (or_4_out, and_8_out, and_5_out);
  or or_5 (or_5_out, and_6_out, and_9_out);
  or or_6 (or_6_out, and_9_out, and_7_out);
  J_K_Flip_Flop j_k_ff_1 (.J(or_3_out), .clk(K), .K(or_4_out), .Q(out_6[1]), .reset(CLR));  // open: Qn, preset, en
  J_K_Flip_Flop j_k_ff_2 (.J(or_5_out), .clk(K), .K(or_6_out), .Q(out_6[2]), .reset(CLR));  // open: Qn, preset, en
  J_K_Flip_Flop j_k_ff_3 (.J(or_1_out), .clk(K), .K(or_2_out), .Q(out_6[0]), .reset(CLR));  // open: Qn, preset, en
  and and_10 (Cout, and_1_out, out_6[0], out_6[1], out_6[2]);
endmodule

module PC (
  input  LOAD,
  input  COUNT,
  input  [5:0] IN,
  input  CLK,
  input  CLR,
  output [5:0] Out,
  output Cout
);

  wire n3_bit_parallel_counter_1_cout, n3_bit_parallel_counter_2_cout;

  _3_BIT_Parallel_Counter u_3_bit_parallel_counter_1 (
    .LOAD(LOAD), .COUNT(COUNT), .IN(IN[2:0]), .K(CLK), .CLR(CLR), .out_6(Out[2:0]),
    .Cout(n3_bit_parallel_counter_1_cout));
  _3_BIT_Parallel_Counter u_3_bit_parallel_counter_2 (
    .LOAD(LOAD), .COUNT(n3_bit_parallel_counter_1_cout), .IN(IN[5:3]), .K(CLK), .CLR(CLR), .out_6(Out[5:3]),
    .Cout(n3_bit_parallel_counter_2_cout));
  and and_1 (Cout, n3_bit_parallel_counter_1_cout, n3_bit_parallel_counter_2_cout);
endmodule

module _1_BIT (
  input  LOAD,
  input  COUNT,
  input  IN,
  input  CLK,
  input  CLR,
  output out,
  output cout
);

  wire and_1_out, and_2_out, and_3_out, not_1_out, not_2_out, not_3_out, or_1_out, or_2_out;

  not not_1 (not_1_out, LOAD);
  not not_2 (not_2_out, not_1_out);
  and and_1 (and_1_out, not_1_out, COUNT);
  not not_3 (not_3_out, IN);
  and and_2 (and_2_out, not_2_out, IN);
  and and_3 (and_3_out, not_3_out, not_2_out);
  or or_1 (or_1_out, and_2_out, and_1_out);
  or or_2 (or_2_out, and_3_out, and_1_out);
  J_K_Flip_Flop j_k_ff_1 (.J(or_1_out), .clk(CLK), .K(or_2_out), .Q(out), .reset(CLR));  // open: Qn, preset, en
  and and_4 (cout, out, and_1_out);
endmodule

module MBR (
  input  LOAD,
  input  COUNT,
  input  [30:0] IN,
  input  CLK,
  input  CLR,
  output [30:0] Cout
);

  wire pc_1_cout, pc_2_cout, pc_3_cout, pc_4_cout, pc_5_cout;

  PC pc_1 (.LOAD(LOAD), .COUNT(COUNT), .IN(IN[5:0]), .CLK(CLK), .CLR(CLR), .Out(Cout[5:0]), .Cout(pc_1_cout));
  PC pc_2 (.LOAD(LOAD), .COUNT(pc_1_cout), .IN(IN[11:6]), .CLK(CLK), .CLR(CLR), .Out(Cout[11:6]), .Cout(pc_2_cout));
  PC pc_3 (.LOAD(LOAD), .COUNT(pc_2_cout), .IN(IN[17:12]), .CLK(CLK), .CLR(CLR), .Out(Cout[17:12]), .Cout(pc_3_cout));
  PC pc_4 (.LOAD(LOAD), .COUNT(pc_3_cout), .IN(IN[23:18]), .CLK(CLK), .CLR(CLR), .Out(Cout[23:18]), .Cout(pc_4_cout));
  PC pc_5 (.LOAD(LOAD), .COUNT(pc_4_cout), .IN(IN[29:24]), .CLK(CLK), .CLR(CLR), .Out(Cout[29:24]), .Cout(pc_5_cout));
  _1_BIT u_1_bit_1 (.LOAD(LOAD), .COUNT(pc_5_cout), .IN(IN[30]), .CLK(CLK), .CLR(CLR), .out(Cout[30]));  // open: cout
endmodule

// MAR
module MAR_CPU (
  input  PC_MAR,
  input  B_MAR,
  input  [5:0] PC_OUT,
  input  [5:0] Address,
  input  CLK,
  input  Reset,
  output [5:0] MAR_OUT,
  output out_8,
  output out_9
);

  wire or_1_out;
  wire [5:0] multiplexer_1_out;

  or or_1 (or_1_out, PC_MAR, B_MAR);
  Multiplexer #(.width(6), .enable("false")) multiplexer_1 (
    .in0(PC_OUT), .in1(Address), .out(multiplexer_1_out), .sel(B_MAR));
  MAR mar_1 (.LOAD(or_1_out), .IN(multiplexer_1_out), .CLK(CLK), .Clr(Reset), .out_5(MAR_OUT));

  assign out_8 = CLK;
  assign out_9 = Reset;
endmodule

// IR
module IR_CPU (
  input  B_IR,
  input  [3:0] OPCODE,
  input  CLK,
  input  Reset,
  output [3:0] IR
);

  IR ir_1 (.LOAD(B_IR), .L1(OPCODE), .CLK(CLK), .CLR(Reset), .out(IR));
endmodule

// MBR
module MBR_CPU (
  input  CLK,
  input  Reset,
  input  M_B,
  input  M_B2,
  input  PC_B,
  input  A_B,
  input  INC_B,
  input  [30:0] DATA_IN,
  input  [30:0] NEW_B,
  input  [30:0] ACC_OUT,
  output LOAD,
  output [30:0] b_out,
  output MBR_0
);

  wire or_1_out, or_3_out;
  wire [30:0] multiplexer_1_out;

  or or_1 (or_1_out, M_B, M_B2);
  or or_2 (LOAD, or_1_out, PC_B, A_B);
  Multiplexer #(.select(2), .width(31), .enable("false")) multiplexer_1 (
    .in0(DATA_IN), .in1(NEW_B), .in2(ACC_OUT), .out(multiplexer_1_out), .sel({A_B, PC_B}));  // open: in3
  MBR mbr_1 (.LOAD(LOAD), .COUNT(INC_B), .IN(multiplexer_1_out), .CLK(CLK), .CLR(Reset), .Cout(b_out));
  or or_3 (or_3_out, b_out[0], b_out[1], b_out[2], b_out[3], b_out[4], b_out[5], b_out[6], b_out[7], b_out[8], b_out[9], b_out[10], b_out[11], b_out[12], b_out[13], b_out[14], b_out[15], b_out[16], b_out[17], b_out[18], b_out[19], b_out[20], b_out[21], b_out[22], b_out[23], b_out[24], b_out[25], b_out[26], b_out[27], b_out[28], b_out[29], b_out[30]);
  not not_1 (MBR_0, or_3_out);
endmodule

module CU (
  input  CLK,
  input  Reset,
  input  [30:0] DATA_IN,
  input  [5:0] MAR_IN,
  input  MBR_0,
  input  [30:0] in_6,
  output PC_MAR,
  output B_MAR,
  output [5:0] PC_OUT,
  output M_B,
  output M_B2,
  output PC_B,
  output A_B,
  output INC_B,
  output [30:0] INC_B_2,
  output [30:0] NEW_B,
  output [30:0] ACC_OUT,
  output [30:0] DATA_OUT,
  output STR
);

  wire ADD, ALU_ADD, ALU_AND, ALU_SUB, AND, and_25_out, and_26_out, B_ACC, B_IR, B_M1, B_M2, B_M3, B_PC, BSB,
       BUN, CLK_t, CMP, d_ff_1_qn, DT, EO, EVEN_ODD, F, F1, F2, HALT, INC_PC2, ISZ, LOAD, not_1_out,
       not_3_out, not_4_out, not_5_out, not_6_out, or_1_out, or_2_out, or_3_out, or_5_out, or_6_out,
       or_7_out, or_8_out, or_9_out, or_10_out, RIGHT_SHIFT, RS, SIGN, Store_t, t0, t1, t2, t3, ZERO;
  wire [0:0] and_18_out;
  wire [1:0] counter_1_q;
  wire [3:0] bit_extender_1_out, IR;
  wire [5:0] multiplexer_1_out;
  wire [30:0] ACC_IN, ACC_IN2, ACC_IN3, ACC_OUT2, bit_extender_2_out, multiplexer_3_out, multiplexer_4_out,
       multiplexer_5_out, multiplexer_7_out, n31_bit_alu_2_out_4, SUM;

  not not_1 (not_1_out, F);
  and and_1 (PC_MAR, not_1_out, t0);
  and and_2 (B_MAR, F, t0);
  and and_3 (M_B2, F, or_1_out, t1);
  and and_4 (INC_B, F, ISZ, t2);
  and and_5 (PC_B, F, BSB, t2);
  Counter #(.width(2), .max('h3)) counter_1 (.Q(counter_1_q), .clk(CLK_t), .clr(Reset));  // open: load, D, count, carry
  or or_1 (or_1_out, AND, ADD, LOAD, ISZ, CMP, RS, EO);
  and and_6 (A_B, F, Store_t, t2);
  or or_2 (or_2_out, B_PC, PC_B);
  or or_3 (or_3_out, M_B, INC_PC2, B_M3);
  or or_4 (STR, B_M1, B_M2, B_M3);
  and and_7 (CLK_t, CLK, ~HALT);  // AND_Gate
  Multiplexer #(.width(6), .enable("false")) multiplexer_1 (
    .in0(in_6[5:0]), .in1(MAR_IN), .out(multiplexer_1_out), .sel(PC_B));
  IR ir_1 (.LOAD(B_IR), .L1(in_6[27:24]), .CLK(CLK_t), .CLR(Reset), .out(IR));
  Multiplexer #(.width(31), .enable("false")) multiplexer_2 (.in0(DATA_IN), .in1(in_6), .out(DATA_OUT), .sel(STR));
  _31_BIT_ALU u_31_bit_alu_1 (
    .in_2(ACC_OUT), .in_3(in_6), .in_1({2{ALU_SUB}}), .out_8(SIGN), .out_4(SUM));  // open: out_5, out_6, out_7
  or or_5 (or_5_out, SUM[0], SUM[1], SUM[2], SUM[3], SUM[4], SUM[5], SUM[6], SUM[7], SUM[8], SUM[9], SUM[10], SUM[11], SUM[12], SUM[13], SUM[14], SUM[15], SUM[16], SUM[17], SUM[18], SUM[19], SUM[20], SUM[21], SUM[22], SUM[23], SUM[24], SUM[25], SUM[26], SUM[27], SUM[28], SUM[29], SUM[30]);
  not not_2 (ZERO, or_5_out);
  Decoder #(.select(2), .enable("false")) decoder_1 (.out0(t0), .out1(t1), .out2(t2), .out3(t3), .sel(counter_1_q));
  PC pc_1 (
    .LOAD(or_2_out), .COUNT(or_3_out), .IN(multiplexer_1_out), .CLK(CLK_t), .CLR(Reset), .Out(NEW_B[5:0]));  // open: Cout
  or or_6 (or_6_out, RIGHT_SHIFT, DT);
  Multiplexer #(.width(31), .enable("false")) multiplexer_3 (
    .in0(ACC_IN), .in1(in_6), .out(multiplexer_3_out), .sel(B_ACC));
  not not_3 (not_3_out, F);
  and and_8 (F1, not_3_out, or_8_out, t3);
  or or_7 (or_7_out, EVEN_ODD, or_6_out, ALU_AND, ALU_ADD, B_ACC);
  Multiplexer #(.width(31), .enable("false")) multiplexer_4 (
    .in0(multiplexer_3_out), .in1(ACC_IN2), .out(multiplexer_4_out), .sel(or_6_out));
  not not_4 (not_4_out, F);
  and and_9 (M_B, not_4_out, t1);
  or or_8 (or_8_out, AND, ADD, Store_t, ISZ, BSB, LOAD, HALT, EO, RS, CMP);
  and and_10 (B_ACC, F, LOAD, t2);
  and and_11 (F2, F, t3);
  Multiplexer #(.width(31), .enable("false")) multiplexer_5 (
    .in0(multiplexer_4_out), .in1(ACC_IN3), .out(multiplexer_5_out), .sel(EVEN_ODD));
  J_K_Flip_Flop j_k_ff_1 (.J(F1), .clk(CLK_t), .K(F2), .Q(F));  // open: Qn, preset, en, reset
  and and_12 (ALU_SUB, F, CMP, t3);
  and and_13 (B_M3, F, BSB, t3);
  and and_14 (B_M1, F, Store_t, t3);
  or or_9 (or_9_out, CMP, or_7_out);
  Decoder #(.select(4), .enable("false")) decoder_2 (
    .out0(AND), .out1(ADD), .out2(Store_t), .out3(ISZ), .out4(BSB), .out5(BUN), .out6(LOAD), .out7(HALT),
    .out8(EO), .out9(RS), .out10(CMP), .sel(IR));  // open: out11, out12, out13, out14, out15
  not not_5 (not_5_out, F);
  and and_15 (B_IR, not_5_out, t2);
  and and_16 (RIGHT_SHIFT, F, RS, t2);
  and and_17 (EVEN_ODD, t2, EO, F);
  or or_10 (or_10_out, ALU_AND, ALU_ADD);
  _31_BIT_ALU u_31_bit_alu_2 (
    .in_2(ACC_OUT), .in_3(in_6), .in_1({ALU_ADD, ALU_AND}), .out_4(n31_bit_alu_2_out_4));  // open: out_5, out_6, out_7, out_8
  AC ac_1 (.LOAD(or_9_out), .IN(multiplexer_5_out), .CLK(CLK_t), .CLR(Reset), .out_5(ACC_OUT));
  and and_18 (and_18_out[0], t3, or_10_out);
  assign bit_extender_1_out = {{3{1'b0}}, PC_B};  // Bit_Extender bit_extender_1
  and and_19 (INC_PC2, F, ISZ, t3, MBR_0);
  and and_20 (ALU_ADD, F, ADD, t3);
  and and_21 (B_M2, F, ISZ, t3);
  Multiplexer #(.select(2), .width(31), .enable("false")) multiplexer_6 (
    .in0(ACC_OUT), .in1(n31_bit_alu_2_out_4), .in2(ACC_OUT2), .out(ACC_IN), .sel({CMP, and_18_out[0]}));  // open: in3
  assign NEW_B[27:24] = bit_extender_1_out & 4'b0101;  // AND_Gate and_22, 4 bits wide
  and and_23 (ALU_AND, F, AND, t3);
  Multiplexer #(.width(31), .enable("false")) multiplexer_7 (
    .in0(ACC_OUT), .in1(in_6), .out(multiplexer_7_out), .sel(SIGN));
  and and_24 (B_PC, BUN, t3);
  D_Flip_Flop d_ff_1 (.clk(CLK_t), .D(RIGHT_SHIFT), .Q(DT), .Qn(d_ff_1_qn), .preset(DT));  // open: en, reset
  and and_25 (and_25_out, EVEN_ODD, 1'b1);
  not not_6 (not_6_out, t2);
  and and_26 (and_26_out, d_ff_1_qn, not_6_out);
  Shift_Register #(.length(31)) shift_register_1 (
    .shift(RIGHT_SHIFT), .in(1'b0), .clk(CLK_t), .load(and_26_out), .clr(Reset), .d0(ACC_OUT[30]),
    .q0(ACC_IN2[30]), .d1(ACC_OUT[29]), .q1(ACC_IN2[29]), .d2(ACC_OUT[28]), .q2(ACC_IN2[28]),
    .d3(ACC_OUT[27]), .q3(ACC_IN2[27]), .d4(ACC_OUT[26]), .q4(ACC_IN2[26]), .d5(ACC_OUT[25]),
    .q5(ACC_IN2[25]), .d6(ACC_OUT[24]), .q6(ACC_IN2[24]), .d7(ACC_OUT[23]), .q7(ACC_IN2[23]),
    .d8(ACC_OUT[22]), .q8(ACC_IN2[22]), .d9(ACC_OUT[21]), .q9(ACC_IN2[21]), .d10(ACC_OUT[20]),
    .q10(ACC_IN2[20]), .d11(ACC_OUT[19]), .q11(ACC_IN2[19]), .d12(ACC_OUT[18]), .q12(ACC_IN2[18]),
    .d13(ACC_OUT[17]), .q13(ACC_IN2[17]), .d14(ACC_OUT[16]), .q14(ACC_IN2[16]), .d15(ACC_OUT[15]),
    .q15(ACC_IN2[15]), .d16(ACC_OUT[14]), .q16(ACC_IN2[14]), .d17(ACC_OUT[13]), .q17(ACC_IN2[13]),
    .d18(ACC_OUT[12]), .q18(ACC_IN2[12]), .d19(ACC_OUT[11]), .q19(ACC_IN2[11]), .d20(ACC_OUT[10]),
    .q20(ACC_IN2[10]), .d21(ACC_OUT[9]), .q21(ACC_IN2[9]), .d22(ACC_OUT[8]), .q22(ACC_IN2[8]),
    .d23(ACC_OUT[7]), .q23(ACC_IN2[7]), .d24(ACC_OUT[6]), .q24(ACC_IN2[6]), .d25(ACC_OUT[5]),
    .q25(ACC_IN2[5]), .d26(ACC_OUT[4]), .q26(ACC_IN2[4]), .d27(ACC_OUT[3]), .q27(ACC_IN2[3]),
    .d28(ACC_OUT[2]), .q28(ACC_IN2[2]), .d29(ACC_OUT[1]), .q29(ACC_IN2[1]), .d30(ACC_OUT[0]), .q30(ACC_IN2[0]));  // open: out
  assign bit_extender_2_out = {{30{1'b0}}, and_25_out};  // Bit_Extender bit_extender_2
  AC ac_2 (.LOAD(CMP), .IN(multiplexer_7_out), .CLK(CLK_t), .CLR(Reset), .out_5(ACC_OUT2));
  _31_BIT_AND u_31_bit_and_1 (.in_1(ACC_OUT), .in_2(bit_extender_2_out), .out_3(ACC_IN3));

  assign INC_B_2 = DATA_IN;
  assign {NEW_B[30:28], NEW_B[23:6]} = {21{1'b0}};
  assign PC_OUT = NEW_B[5:0];

  // Other names for the same wires on the sheet: Address[5:0] = in_6[5:0]; b_out[30:0] = in_6;
  //   OPCODE[3:0] = in_6[27:24]; INC_PC1 = M_B; INC_PC3 = B_M3; MAR_OUT[5:0] = MAR_IN; B_OP = PC_B; MAR_PC = PC_B;
  //   STORE = STR

  // Notes on the sheet:
  //   F0t0
  //   mem to mbr 2
  //   execution cycle 
  //   F0t1
  //   transfer operation code
endmodule

module CPU (
  input  in_1
);

  wire CLK, cu_1_a_b, cu_1_b_mar, cu_1_inc_b, cu_1_m_b, cu_1_m_b2, cu_1_pc_b, cu_1_pc_mar, LOAD,
       mar_cpu_1_out_8, mar_cpu_1_out_9, MBR_0, Store;
  wire [5:0] cu_1_pc_out, mar_cpu_1_mar_out;
  wire [30:0] cu_1_acc_out, cu_1_data_out, cu_1_inc_b_2, cu_1_new_b, mbr_cpu_1_b_out, ram_1_data;

  Clock u_Clk (.out(CLK));
  CU cu_1 (
    .DATA_IN(ram_1_data), .MAR_IN(mar_cpu_1_mar_out), .MBR_0(MBR_0), .CLK(CLK), .Reset(in_1),
    .DATA_OUT(cu_1_data_out), .in_6(mbr_cpu_1_b_out), .PC_MAR(cu_1_pc_mar), .B_MAR(cu_1_b_mar),
    .PC_OUT(cu_1_pc_out), .M_B(cu_1_m_b), .M_B2(cu_1_m_b2), .PC_B(cu_1_pc_b), .A_B(cu_1_a_b),
    .INC_B(cu_1_inc_b), .INC_B_2(cu_1_inc_b_2), .NEW_B(cu_1_new_b), .ACC_OUT(cu_1_acc_out), .STR(Store));
  MAR_CPU mar_cpu_1 (
    .PC_MAR(cu_1_pc_mar), .B_MAR(cu_1_b_mar), .PC_OUT(cu_1_pc_out), .Address(mbr_cpu_1_b_out[5:0]),
    .CLK(CLK), .Reset(in_1), .out_8(mar_cpu_1_out_8), .out_9(mar_cpu_1_out_9), .MAR_OUT(mar_cpu_1_mar_out));
  MBR_CPU mbr_cpu_1 (
    .M_B(cu_1_m_b), .M_B2(cu_1_m_b2), .PC_B(cu_1_pc_b), .A_B(cu_1_a_b), .INC_B(cu_1_inc_b),
    .DATA_IN(cu_1_inc_b_2), .NEW_B(cu_1_new_b), .ACC_OUT(cu_1_acc_out), .CLK(mar_cpu_1_out_8),
    .Reset(mar_cpu_1_out_9), .LOAD(LOAD), .b_out(mbr_cpu_1_b_out), .MBR_0(MBR_0));
  RAM #(.addrWidth(6), .dataWidth(31), .bus("separate")) ram_1 (
    .addr(mar_cpu_1_mar_out), .din(cu_1_data_out), .data(ram_1_data), .str(Store), .clk(CLK), .ld(LOAD));  // open: sel, clr

  // Other names for the same wires on the sheet: Reset = in_1
endmodule
